# Fritzing sketch game (saved by Fritzing 0.9.3b)
circuit board: 8.46667cm x 5.64444cm
breadboards: 2

parts:
  IC1 = Atmega328-P [package=dil28-3-simon]
  C1 = Ceramic Capacitor [capacitance=100nF package="100 mil [THT, multilayer]"]
  C2 = Ceramic Capacitor [capacitance=100nF package="100 mil [THT, multilayer]"]
  XTAL1 = Crystal [frequency="16 Mhz" package=THT]

nets:
  N1: IC1.GND, C1.1, C2.1
  N2: IC1.PB6(XTAL1_TOSC1), C1.0, XTAL1.pin_1
  N3: IC1.PB7(XTAL2_TOSC2), C2.0, XTAL1.pin_0

custom parts:
  Atmega328-P: MICROCONTROLLER 32 KB FLASH 2 KB SRAM 1KB EEPROM USART 4-channel 10 bit ADC 2-channel 8 bit ADC
