# Fritzing sketch atmega329p (saved by Fritzing 0.9.3b)
circuit board: 8.46667cm x 5.64444cm
breadboards: 1

parts:
  IC1 = Atmega328-P [package=dil28-3-simon]
  Y1 = CRYSTAL [part_number=16Mhz package=hc49u-v]
  C1 = Ceramic Capacitor [capacitance=0.22m part_number=22ppf package="0603 [SMD, multilayer]"]
  C2 = Ceramic Capacitor [capacitance="100 nF" package="0603 [SMD, multilayer]"]
  R1 = Resistor [tolerance=±5% resistance=10k package="0402 [SMD]"]

nets (from the pcb view):
  N1: IC1.PC6(_RESET), R1.Pin_0
  N2: IC1.VCC, R1.Pin_1
  N3: IC1.GND, IC1.PB6(XTAL1_TOSC1), IC1.PB7(XTAL2_TOSC2), Y1.1, Y1.2, C1.0, C1.1, C2.0, C2.1
  N4: IC1.AVCC, IC1.AREF

notes:
  22pf capacitors
  16 Mhz crystal
  10K resistor

custom parts:
  Atmega328-P: MICROCONTROLLER 32 KB FLASH 2 KB SRAM 1KB EEPROM USART 4-channel 10 bit ADC 2-channel 8 bit ADC
